// Logisim project cpu.circ as structural Verilog: 3 circuits, main circuit main
module main (
  input  [31:0] INSTRUCTION,
  input  CLOCK,
  output [31:0] FETCH_ADDRESS,
  output [31:0] s0_Value,
  output [31:0] s1_Value,
  output [31:0] s2_Value,
  output [31:0] ra_Value,
  output [31:0] sp_Value
);

  wire adder_1_cout, ALUSrc, and_1_out, and_2_out, and_3_out, extOp, flushPipeline, isbeq, isbne, isbov,
       isequal, isJ, isJal, isJalr, isJr, isLui, isoverflow, isShift, jump, main_3_p1, main_3_p2, memR,
       memReg, memWr, not_1_out, or_4_out, or_5_out, regDst, regWr, takeBranch, takeJump;
  wire [1:0] ALUop;
  wire [3:0] ALUCtr;
  wire [4:0] multiplexer_2_out, writeReg;
  wire [5:0] funct;
  wire [15:6] imm;
  wire [25:16] jumpaddr;
  wire [27:0] bit_extender_4_out, PCJump;
  wire [31:0] ALUx, bit_extender_1_out, bit_extender_2_out, bit_extender_3_out, immExtend, main_2_result,
       main_3_p7, multiplexer_1_out, multiplexer_6_out, multiplexer_7_out, multiplexer_8_out,
       multiplexer_10_out, multiplexer_11_out, nextPC, PC_4, PCBranch, PCJr, shifter_1_out, write_Data,
       writeData;
  wire [31:26] newInstr;

  Multiplexer #(.width(32)) multiplexer_1 (
    .in0(INSTRUCTION), .in1({32{1'b0}}), .out(multiplexer_1_out), .sel(flushPipeline));  // open: en
  control_unit control_unit_1 (
    .instruction(newInstr), .jump(jump), .extOp(extOp), .regDst(regDst), .ALUSrc(ALUSrc), .ALUop(ALUop),
    .memWr(memWr), .memR(memR), .memReg(memReg), .regWr(regWr), .isLui(isLui), .isbeq(isbeq), .isJal(isJal),
    .isbne(isbne), .isJ(isJ), .isbov(isbov));
  Register #(.width(32)) pipelineReg (
    .D(multiplexer_1_out), .Q({newInstr, jumpaddr, imm, funct}), .clk(CLOCK));  // open: en, clr
  not not_1 (not_1_out, isequal);
  // Probe on {newInstr, jumpaddr, imm, funct}
  and and_1 (and_1_out, isbeq, isequal);
  and and_2 (and_2_out, isbne, not_1_out);
  and and_3 (and_3_out, isbov, isoverflow);
  or or_1 (takeJump, isJr, isJalr, isJal, isJ);
  or or_2 (flushPipeline, takeJump, takeBranch);
  or or_3 (takeBranch, and_1_out, and_2_out, and_3_out);
  ALUcontrol_unit alucontrol_unit_1 (
    .\function (funct), .ALUop(ALUop), .opcode(newInstr), .ALUCtr(ALUCtr), .isShift(isShift), .isJr(isJr),
    .isJalr(isJalr));
  assign bit_extender_1_out = {{27{imm[10]}}, imm[10:6]};  // Bit_Extender bit_extender_1
  Multiplexer #(.width(5)) multiplexer_2 (
    .in0(jumpaddr[20:16]), .in1(imm[15:11]), .out(multiplexer_2_out), .sel(regDst));  // open: en
  assign bit_extender_2_out = {{16{1'b0}}, {imm, funct}};  // Bit_Extender bit_extender_2
  assign bit_extender_3_out = {{16{imm[15]}}, {imm, funct}};  // Bit_Extender bit_extender_3
  regfile_main main_1 (
    .Read_Register_1(jumpaddr[25:21]), .Read_Register_2(jumpaddr[20:16]), .Write_Register(writeReg),
    .Write_Data(writeData), .Write_Enable(regWr), .Clock(CLOCK), .Read_Data_1(PCJr),
    .Read_Data_2(write_Data), .s0_Value(s0_Value), .s1_Value(s1_Value), .s2_Value(s2_Value),
    .ra_Value(ra_Value), .sp_Value(sp_Value));
  Multiplexer #(.width(32)) multiplexer_3 (
    .in0(PCJr), .in1(bit_extender_1_out), .out(ALUx), .sel(isShift));  // open: en
  Multiplexer #(.width(5)) multiplexer_4 (
    .in0(multiplexer_2_out), .in1({5{1'b1}}), .out(writeReg), .sel(isJal));  // open: en
  Multiplexer #(.width(32)) multiplexer_5 (
    .in0(bit_extender_2_out), .in1(bit_extender_3_out), .out(immExtend), .sel(extOp));  // open: en
  Multiplexer #(.width(32)) multiplexer_6 (
    .in0(PC_4), .in1(PCBranch), .out(multiplexer_6_out), .sel(takeBranch));  // open: en
  Multiplexer #(.width(32)) multiplexer_7 (
    .in0(write_Data), .in1(immExtend), .out(multiplexer_7_out), .sel(ALUSrc));  // open: en
  // Probe on nextPC
  Adder #(.width(32)) adder_1 (.a(FETCH_ADDRESS), .b(32'h4), .out(PC_4), .cout(adder_1_cout));  // open: cin
  // Probe on PC_4
  assign bit_extender_4_out = {{2{1'b0}}, {jumpaddr, imm, funct}};  // Bit_Extender bit_extender_4
  // Probe on multiplexer_6_out
  or or_4 (or_4_out, isJ, isJal);
  LED led_1 (.in(isoverflow));
  alu_main main_2 (
    .Switch(ALUCtr), .X(ALUx), .Equal(isequal), .Result(main_2_result), .Signed_Overflow(isoverflow),
    .Y(multiplexer_7_out));
  // Probe on ALUCtr
  Register #(.width(32)) PC (.D(nextPC), .Q(FETCH_ADDRESS), .clk(CLOCK));  // open: en, clr
  Shifter #(.width(32)) shifter_1 (.in(immExtend), .\dist (5'b00010), .out(shifter_1_out));
  Shifter #(.width(28)) shifter_2 (.in(bit_extender_4_out), .\dist (5'b00010), .out(PCJump));
  Multiplexer #(.width(32)) multiplexer_8 (
    .in0(multiplexer_6_out), .in1({PC_4[31:28], PCJump}), .out(multiplexer_8_out), .sel(or_4_out));  // open: en
  // Probe on PCJr
  // Probe on PCBranch
  Adder #(.width(32)) adder_2 (.a(FETCH_ADDRESS), .b(shifter_1_out), .out(PCBranch));  // open: cin, cout
  // Probe on {PC_4[31:28], PCJump}
  Multiplexer #(.width(32)) multiplexer_9 (
    .in0(multiplexer_8_out), .in1(PCJr), .out(nextPC), .sel(or_5_out));  // open: en
  or or_5 (or_5_out, isJr, isJalr);
  // mem_main main_3: pin names not known; wires that end beside it: main_3_p1, main_3_p2, main_2_result, write_Data, memWr, CLOCK, main_3_p7
  Multiplexer #(.width(32)) multiplexer_10 (
    .in0(main_2_result), .in1(main_3_p7), .out(multiplexer_10_out), .sel(memReg));  // open: en
  // Probe on FETCH_ADDRESS
  Multiplexer #(.width(32)) multiplexer_11 (
    .in0(multiplexer_10_out), .in1(FETCH_ADDRESS), .out(multiplexer_11_out), .sel(isJal));  // open: en
  // Probe on writeData
  Multiplexer #(.width(32)) multiplexer_12 (
    .in0(multiplexer_11_out), .in1({imm, funct, {16{1'b0}}}), .out(writeData), .sel(isLui));  // open: en

  // Other names for the same wires on the sheet: clk = CLOCK; fetch_addr[31:0] = FETCH_ADDRESS;
  //   PC[31:0] = FETCH_ADDRESS; imm[5:0] = funct; immLui[31:16] = {imm, funct}; jumpaddr[15:0] = {imm, funct};
  //   newInstr[25:0] = {jumpaddr, imm, funct}; shamt[4:0] = imm[10:6]; rd[4:0] = imm[15:11];
  //   readReg2[4:0] = jumpaddr[20:16]; rt[4:0] = jumpaddr[20:16]; readReg1[4:0] = jumpaddr[25:21];
  //   rs[4:0] = jumpaddr[25:21]; opcode[5:0] = newInstr; PCJump[31:28] = PC_4[31:28]; ra[31:0] = ra_Value;
  //   s0[31:0] = s0_Value; s1[31:0] = s1_Value; s2[31:0] = s2_Value; shiftX[31:0] = PCJr; sp[31:0] = sp_Value

  // Notes on the sheet:
  //   Output
  //   These are outputs/inputs from run.circ
  //   Inputs
  //   These are DEBUG/TEST outputs from your circuit.
endmodule

module control_unit (
  input  [5:0] instruction,
  output jump,
  output extOp,
  output regDst,
  output ALUSrc,
  output [1:0] ALUop,
  output memWr,
  output memR,
  output memReg,
  output regWr,
  output isLui,
  output isbeq,
  output isJal,
  output isbne,
  output isJ,
  output isbov
);

  wire [9:0] multiplexer_1_out, multiplexer_3_out;

  Multiplexer #(.select(5), .width(10)) multiplexer_1 (
    .in0(10'h81), .in2(10'h210), .in3(10'h211), .in4(10'h100), .in5(10'h100), .in6(10'h110), .in8(10'h151),
    .in9(10'h151), .in10(10'h16f), .in11(10'h16f), .in12(10'h59), .in13(10'h41), .in15(10'h157),
    .out(multiplexer_1_out), .sel(instruction[4:0]));  // open: in1, in7, in14, in16, in17, in18, in19, in20, in21, in22, in23, in24, in25, in26, in27, in28, in29, in30, in31, en
  Comparator #(.width(6), .mode("unsigned")) comparator_1 (.a(instruction), .b(6'b000011), .eq(isJal));  // open: gt, lt
  Comparator #(.width(6), .mode("unsigned")) comparator_2 (.a(instruction), .b(6'b000010), .eq(isJ));  // open: gt, lt
  Multiplexer #(.width(10)) multiplexer_2 (
    .in0(multiplexer_1_out), .in1(multiplexer_3_out),
    .out({jump, extOp, regDst, ALUSrc, ALUop, memWr, memR, memReg, regWr}), .sel(instruction[5]));  // open: en
  Multiplexer #(.select(5), .width(10)) multiplexer_3 (
    .in3(10'h157), .in11(10'h158), .out(multiplexer_3_out), .sel(instruction[4:0]));  // open: in0, in1, in2, in4, in5, in6, in7, in8, in9, in10, in12, in13, in14, in15, in16, in17, in18, in19, in20, in21, in22, in23, in24, in25, in26, in27, in28, in29, in30, in31, en
  Comparator #(.width(6), .mode("unsigned")) comparator_3 (.a(instruction), .b(6'b001111), .eq(isLui));  // open: gt, lt
  Comparator #(.width(6), .mode("unsigned")) comparator_4 (.a(instruction), .b(6'b000100), .eq(isbeq));  // open: gt, lt
  Comparator #(.width(6), .mode("unsigned")) comparator_5 (.a(instruction), .b(6'b000101), .eq(isbne));  // open: gt, lt
  Comparator #(.width(6), .mode("unsigned")) comparator_6 (.a(instruction), .b(6'b000110), .eq(isbov));  // open: gt, lt

  // Other names for the same wires on the sheet: _1_32[4:0] = instruction[4:0]; instr[5:0] = instruction;
  //   _0_or_1 = instruction[5]
endmodule

module ALUcontrol_unit (
  input  [5:0] opcode,
  input  [5:0] \function ,
  input  [1:0] ALUop,
  output [3:0] ALUCtr,
  output isShift,
  output isJr,
  output isJalr
);

  wire and_1_out, and_2_out, and_3_out, comparator_1_eq, comparator_2_eq, comparator_3_eq, comparator_4_eq,
       comparator_5_eq, comparator_6_eq, comparator_7_eq;
  wire [3:0] ALUfunc, multiplexer_1_out, multiplexer_3_out;

  Multiplexer #(.select(5), .width(4)) multiplexer_1 (
    .in0(4'b0000), .in2(4'b0001), .in3(4'b0010), .in8(4'b1101), .in9(4'b1101), .out(multiplexer_1_out),
    .sel(\function [4:0]));  // open: in1, in4, in5, in6, in7, in10, in11, in12, in13, in14, in15, in16, in17, in18, in19, in20, in21, in22, in23, in24, in25, in26, in27, in28, in29, in30, in31, en
  Multiplexer #(.width(4)) multiplexer_2 (
    .in0(multiplexer_1_out), .in1(multiplexer_3_out), .out(ALUfunc), .sel(\function [5]));  // open: en
  Multiplexer #(.select(5), .width(4)) multiplexer_3 (
    .in0(4'b0101), .in1(4'b0110), .in2(4'b0111), .in3(4'b1000), .in4(4'b1001), .in5(4'b1010), .in10(4'b1011),
    .in11(4'b1100), .out(multiplexer_3_out), .sel(\function [4:0]));  // open: in6, in7, in8, in9, in12, in13, in14, in15, in16, in17, in18, in19, in20, in21, in22, in23, in24, in25, in26, in27, in28, in29, in30, in31, en
  Multiplexer #(.select(2), .width(4)) multiplexer_4 (
    .in0(ALUfunc), .in1(4'b0101), .in2(4'b0111), .out(ALUCtr), .sel(ALUop));  // open: in3, en
  Comparator #(.width(6), .mode("unsigned")) comparator_1 (
    .a(\function ), .b({6{1'b0}}), .eq(comparator_1_eq));  // open: gt, lt
  Comparator #(.width(6), .mode("unsigned")) comparator_2 (
    .a(\function ), .b(6'b000010), .eq(comparator_2_eq));  // open: gt, lt
  Comparator #(.width(6), .mode("unsigned")) comparator_3 (
    .a(\function ), .b(6'b000011), .eq(comparator_3_eq));  // open: gt, lt
  Comparator #(.width(6), .mode("unsigned")) comparator_4 (
    .a(opcode), .b({6{1'b0}}), .eq(comparator_4_eq));  // open: gt, lt
  Comparator #(.width(6), .mode("unsigned")) comparator_5 (
    .a(\function ), .b(6'b001000), .eq(comparator_5_eq));  // open: gt, lt
  Comparator #(.width(6), .mode("unsigned")) comparator_6 (
    .a(\function ), .b(6'b001001), .eq(comparator_6_eq));  // open: gt, lt
  Comparator #(.width(6), .mode("unsigned")) comparator_7 (
    .a(opcode), .b({6{1'b0}}), .eq(comparator_7_eq));  // open: gt, lt
  and and_1 (and_1_out, comparator_1_eq, comparator_4_eq);
  and and_2 (and_2_out, comparator_2_eq, comparator_4_eq);
  and and_3 (and_3_out, comparator_3_eq, comparator_4_eq);
  and and_4 (isJr, comparator_5_eq, comparator_7_eq);
  and and_5 (isJalr, comparator_6_eq, comparator_7_eq);
  or or_1 (isShift, and_1_out, and_2_out, and_3_out);

  // Other names for the same wires on the sheet: _1_32_2[4:0] = \function [4:0]; _0_or_1_2 = \function [5];
  //   opc[5:0] = opcode
endmodule
