// Logisim project alu.circ as structural Verilog: 1 circuit, main circuit main
module main (
  input  [31:0] X,
  input  [31:0] Y,
  input  [3:0] Switch,
  output Signed_Overflow,
  output Equal,
  output [31:0] Result
);

  wire addcarryout_bit, adder_3_cout, adder_4_cout, and_2_out, and_3_out, comparator_1_lt, comparator_2_lt,
       comparator_4_eq, comparator_5_eq, comparator_6_eq, comparator_7_eq, not_1_out, not_2_out,
       subcarryout_bit;
  wire [4:0] bit_extender_3_out;
  wire [31:0] add, addu, \and , \or , shifter_1_out, shifter_2_out, sll, slt, sltu, sra, srl, sub, subu;

  assign \and  = X & Y;  // AND_Gate and_1, 32 bits wide
  assign \or  = X | Y;  // OR_Gate or_1, 32 bits wide
  Adder #(.width(32)) adder_1 (.a(X), .b(Y), .out(addu));  // open: cin, cout
  Subtractor #(.width(32)) subtractor_1 (.a(X), .b(Y), .out(subu));  // open: bin, bout
  Comparator #(.width(32)) comparator_1 (.a(X), .b(Y), .lt(comparator_1_lt));  // open: gt, eq
  Comparator #(.width(32), .mode("unsigned")) comparator_2 (.a(X), .b(Y), .lt(comparator_2_lt));  // open: gt, eq
  Comparator #(.width(32)) comparator_3 (.a(X), .b(Y), .eq(Equal));  // open: gt, lt
  assign slt = {{31{1'b0}}, comparator_1_lt};  // Bit_Extender bit_extender_1
  assign sltu = {{31{1'b0}}, comparator_2_lt};  // Bit_Extender bit_extender_2
  Bit_Extender #(.in_width(32), .out_width(5)) bit_extender_3 (.in(X), .out(bit_extender_3_out));
  Shifter #(.width(32)) shifter_1 (.in(X), .\dist (5'b00001), .out(shifter_1_out));
  Shifter #(.width(32)) shifter_2 (.in(Y), .\dist (5'b00001), .out(shifter_2_out));
  Adder #(.width(32)) adder_2 (.a(X), .b(Y), .out(add), .cout(addcarryout_bit));  // open: cin
  Subtractor #(.width(32)) subtractor_2 (.a(X), .b(Y), .out(sub), .bout(subcarryout_bit));  // open: bin
  Multiplexer #(.select(4), .width(32)) multiplexer_1 (
    .in0(sll), .in1(srl), .in2(sra), .in5(add), .in6(addu), .in7(sub), .in8(subu), .in9(\and ), .in10(\or ),
    .in11(slt), .in12(sltu), .out(Result), .sel(Switch));  // open: in3, in4, in13, in14, in15, en
  Shifter #(.width(32)) shifter_3 (.in(Y), .\dist (bit_extender_3_out), .out(sll));
  Shifter #(.width(32), .shift("lr")) shifter_4 (.in(Y), .\dist (bit_extender_3_out), .out(srl));
  Shifter #(.width(32), .shift("ar")) shifter_5 (.in(Y), .\dist (bit_extender_3_out), .out(sra));
  Adder #(.width(32)) adder_3 (.a(shifter_1_out), .b(shifter_2_out), .cout(adder_3_cout));  // open: out, cin
  Adder #(.width(32)) adder_4 (.a(shifter_1_out), .b(shifter_2_out), .cout(adder_4_cout));  // open: out, cin
  Comparator #(.width(1)) comparator_4 (.a(addcarryout_bit), .b(adder_3_cout), .eq(comparator_4_eq));  // open: gt, lt
  Comparator #(.width(4)) comparator_5 (.a(4'b0101), .b(Switch), .eq(comparator_5_eq));  // open: gt, lt
  Comparator #(.width(1)) comparator_6 (.a(subcarryout_bit), .b(adder_4_cout), .eq(comparator_6_eq));  // open: gt, lt
  not not_1 (not_1_out, comparator_4_eq);
  not not_2 (not_2_out, comparator_6_eq);
  Comparator #(.width(4)) comparator_7 (.a(4'b0111), .b(Switch), .eq(comparator_7_eq));  // open: gt, lt
  and and_2 (and_2_out, not_1_out, comparator_5_eq);
  and and_3 (and_3_out, not_2_out, comparator_7_eq);
  or or_2 (Signed_Overflow, and_2_out, and_3_out);

  // Other names for the same wires on the sheet: overflow = Signed_Overflow; S[3:0] = Switch

  // Notes on the sheet:
  //   INPUTS to your circuit
  //   DON'T CHANGE THE LOCATIONS OF THE INPUTS AND OUTPUTS!
  //   OUTPUTS from your circuit
endmodule
